# Fritzing sketch temp_humi_wifi_thingspeak (saved by Fritzing 0.9.3b)
breadboards: 1

parts:
  부품1 = Arduino Uno (Rev3)
  U1 = ESP8266 WiFi Module [part_number=ESP8266]
  Part1 = KY-015 Temperature & Humidity Sensor Module [package="Breakout board"]

nets:
  N1: 부품1.D10_PWM/SS, U1.RXD
  N2: 부품1.D11_PWM/MOSI, U1.TXD
  GND: 부품1.GND, U1.GND, Part1.-
  N3: 부품1.D2, Part1.S
  3V3: 부품1.3V3, U1.VCC, U1.CH_PD
  5V: 부품1.5V, Part1.Vin

notes:
  위에 적은 blog에서 따라하다가 시간 많이 버림; 아래 blog보고 다시함
  ESP8266 Firmware Update 하면서 핀들을 다른데 꽂아야한다.
  "USB to UART"가 있으면 그걸로 ESP8266은 Firmware를 Update하고 연결하면 좋을 것 같다.
  ESP8266 RX/TX를 Arduino RX(D0)/TX(D1)하고 연결해야한다. 이건 Arduino하고 ESP8266간의 통신이 아니고 Computer의 COMx port하고 ESP8266의 통신인데 USB to UART가 없어서 Arduino의 컴퓨터 통신을 이용해서 Arduino를 Bypass하는거다.
  Arduino를 이용해서 Firmware를 update하려면 Arduino controller를 뽑아 내고 GPIO 0를 GND에 연결하면 Flash mode로 바뀜
  http://blog.naver.com/nasu0210/220968507078
  아래에서 주로 보고 따라했지만 Firmware를 Update하는데 좀 문제가 있었다.
  http://cafe.naver.com/makercoop/366
  DHT11 module은 아래 library가 제대로 작동했다.
  https://github.com/markruys/arduino-DHT
  git@github.com:markruys/arduino-DHT.git
  DHT11 sensor가 있고, 4발짜리. DHT11 Module이 있다. 3발짜리..

custom parts:
  ESP8266 WiFi Module: Generic WiFi Module based on the ESP8266 with onboard PCB antenna and UART communications
  KY-015 Temperature & Humidity Sensor Module: KY-015 temperature and humidity sensor module, provides a low-latency serial interface to measure humidity and temperature.

// code stored in the sketch: temp_humi_wifi_thingspeak.ino
#include "DHT.h"
#include <SoftwareSerial.h>

const int dhtPin = 2;
DHT dht;

// ??? thingspeak ??? API key ??
String apiKey = "BKU14NX6Q4BH7VFL";

SoftwareSerial esp8266(11, 10); // RX/TX ??, serial ????

void setup() {  
  Serial.begin(9600);
  Serial.println();
  Serial.println("Status\tHumidity (%)\tTemperature (C)\t(F)");

  dht.setup(dhtPin);

  esp8266.begin(9600);        //????? ??? ??
  esp8266.println("AT+RST");  //ESP8266 Reset
}

void loop() {
  delay(dht.getMinimumSamplingPeriod());

  float humidity = dht.getHumidity();
  float temperature = dht.getTemperature();

  Serial.print(dht.getStatusString());
  Serial.print("\t");
  Serial.print(humidity, 1);
  Serial.print("\t\t");
  Serial.print(temperature, 1);
  Serial.print("\t\t");
  Serial.println(dht.toFahrenheit(temperature), 1);

  // String ??
  char humidity_buffer[16];
  String strHumi = dtostrf(humidity, 4, 1, humidity_buffer);
  char temperature_buffer[16];
  String strTemp = dtostrf(temperature, 4, 1, temperature_buffer);

  // TCP ??
  String cmd = "AT+CIPSTART=\"TCP\",\"";
  cmd += "184.106.153.149"; // api.thingspeak.com ?? IP
  cmd += "\",80";           // api.thingspeak.com ?? ??, 80
  esp8266.println(cmd);
   
  if(esp8266.find("Error")){
    Serial.println("AT+CIPSTART error");
    return;
  }
  
  // GET ???? ??? ?? String, Data ??
  String getStr = "GET /update?api_key=";
  getStr += apiKey;
  getStr +="&field1=";
  getStr += String(strTemp);
  getStr +="&field2=";
  getStr += String(strHumi);
  getStr += "\r\n\r\n";
 
  // Send Data
  cmd = "AT+CIPSEND=";
  cmd += String(getStr.length());
  esp8266.println(cmd);
 
  if(esp8266.find(">")) esp8266.print(getStr);
  else {
    esp8266.println("AT+CIPCLOSE");
    Serial.println("AT+CIPCLOSE");  // alert user
  }

  delay(20000); // Thingspeak ?? ??? ?? 15?? ??? ?? delay
}
